# Fritzing sketch wiring (saved by Fritzing 0.9.3b)

parts:
  DC_Mot_Enc1 = DC Motor with two-phase hall-encoder [part_number=VT-E-G25A-06-177E]
  M1 = MDD10A
  DC_Mot_Enc2 = DC Motor with two-phase hall-encoder [part_number=VT-E-G25A-06-177E]
  VCC1 = 4 x AAA Battery Mount
  Composant2 = Arduino Nano RP2040 Connect
  J1 = Infrared Proximity Sensor
  J2 = Infrared Proximity Sensor
  S1 = Pushbutton [package="[THT]"]
  S2 = Pushbutton [package="[THT]"]
  R1 = Resistor [tolerance=±5% resistance=220 package=THT]
  R2 = Resistor [tolerance=±5% resistance=220 package=THT]
  J3 = female pin header, 1 pin [form="♀ (female)"]
  J4 = female pin header, 1 pin [form="♀ (female)"]
  Raspberry_Pi_1 = Raspberry Pi 3 [part_number=RPI-3-V1.2]
  S3 = Toggle Switch [package=THT]
  J5 = female pin header, 1 pin [form="♀ (female)"]
  J6 = female pin header, 1 pin [form="♀ (female)"]
  J7 = female pin header, 1 pin [form="♀ (female)"]
  J8 = female pin header, 1 pin [form="♀ (female)"]
  S4 = Pushbutton [package="[THT]"]
  D1 = Rectifier Diode [part_number=1N4001 package="300 mil [THT]"]
  A1 = ina226 module
  S5 = 0.91 inch OLED I2C Display 128 x 32 Pixels

nets:
  N1: DC_Mot_Enc1.pin1, M1.M1A1
  N2: DC_Mot_Enc1.pin2, M1.M1B-1
  VCC: DC_Mot_Enc1.pin3, M1.M2A-1, DC_Mot_Enc2.pin2, DC_Mot_Enc2.pin3, Composant2.3V3, J1.Vcc, J2.Vcc, S1.Pin_3, S2.Pin_1, S2.Pin_2, J4.pin1, A1.Pin_8, S5.VCC
  N3: DC_Mot_Enc1.pin4, Composant2.D6/GPIO18
  N4: DC_Mot_Enc1.pin5, Composant2.D7/GPIO19
  GND: DC_Mot_Enc1.pin6, M1.Bat-, M1.GND, DC_Mot_Enc2.pin6, VCC1.-, Composant2.GND, J1.GND, J2.GND, R1.Pin_0, R2.Pin_0, J3.pin1, J5.pin1, J6.pin1, A1.Pin_7, S5.GND
  N5: M1.Bat+, J7.pin1, S4.Pin_1, S4.Pin_2
  N6: M1.M2B-1, DC_Mot_Enc2.pin1
  N7: M1.PWM2, Composant2.D4/GPIO16
  N8: M1.DIR2, Composant2.D5/GPIO17
  N9: M1.PWM1, Composant2.D8/GPIO20
  N10: M1.DIR1, Composant2.D9/GPIO21
  N11: DC_Mot_Enc2.pin4, Composant2.D3/GPIO15
  N12: DC_Mot_Enc2.pin5, Composant2.D2/GPIO25
  N13: VCC1.+, S3.COM
  N14: Composant2.A0/D14/GPIO26, S2.Pin_3, S2.Pin_4, R2.Pin_1
  N15: Composant2.A1/D15/GPIO27, J1.Vout
  N16: Composant2.A2/D16/GPIO28, S1.Pin_2, R1.Pin_1
  N17: Composant2.A3/D17/GPIO29, J2.Vout
  N18: Composant2.A4/D18/GPIO12, A1.Pin_6, S5.SDA
  N19: Composant2.A5/D19/GPIO13, A1.Pin_5, S5.SCL
  N20: Composant2.VIN, D1.cathode
  N21: Composant2.RX/GPIO1, Raspberry_Pi_1.GIPO12
  N22: Composant2.TX/GPIO0, Raspberry_Pi_1.GND
  N23: S3.L2, A1.Pin_13
  N24: J8.pin1, S4.Pin_3, S4.Pin_4, D1.anode, A1.Pin_2, A1.Pin_12

notes:
  Capteur LIDAR
  Capteur Rotation
  Moteur Droit
  Moteur Gauche
  Encodeur
  Controleur
  Arret d'urgence
  Batterie 6V au plomb
  Rail 3.3V
  Interrupteur Central
  Rail 1 Vbatt (sans l'arret d'urgence)
  Rail 2 Vbatt (avec l'arret d'urgence)
  RAIL I2C
  INA 226

custom parts:
  ina226 module: INA226 Voltage Current/Power Monitoring Sensor Module IIC I2C Interface Bi-directional INA226 Module CJMCU-226.
